# Fritzing sketch pommodoro-timer (saved by Fritzing 0.9.3b)
breadboards: 1

parts:
  Part1 = Arduino Uno (Rev3)
  U1 = LCD-16X2 [part_number="JHD 162A" package=lcd-16x2_noholes]
  S2 = Momentary Switch [package=ksa_sealed_tac_switch]
  R1 = Trimmer Potentiometer [maximum_resistance=10kΩ package=THT]
  R2 = Resistor [tolerance=±5% resistance=220 package="0805 [SMD]"]
  R3 = Resistor [tolerance=±5% resistance=10k package=THT]
  R5 = Resistor [tolerance=±5% resistance=220 package=THT]
  R6 = Resistor [tolerance=±5% resistance=220 package=THT]
  LED1 = LED - 5mm [color="Red (633nm)" package="5 mm [THT]"]
  LED2 = LED - 5mm [color="Green (560nm)" package="5 mm [THT]"]

nets:
  N1: Part1.D9_PWM, S2.3, R3.Pin_1
  N2: Part1.D11_PWM/MOSI, U1.E
  N3: Part1.D12/MISO, U1.RS
  N4: Part1.D2, U1.DB7
  N5: Part1.D3_PWM, U1.DB6
  N6: Part1.D4, U1.DB5
  N7: Part1.D5_PWM, U1.DB4
  N8: Part1.D6_PWM, R5.Pin_1
  N9: Part1.D7, R6.Pin_1
  5V: Part1.5V, U1.VDD, S2.1, R1.leg1, R2.Pin_0
  GND: Part1.GND, U1.VSS, U1.R_W, U1.K, R1.leg2, R3.Pin_0, LED1.cathode, LED2.cathode
  N10: U1.VO, R1.wiper
  N11: U1.A, R2.Pin_1
  N12: R5.Pin_0, LED1.anode
  N13: R6.Pin_0, LED2.anode
